# Fritzing sketch estacao (saved by Fritzing 0.9.2b)
breadboards: 1

parts:
  verde = LED - 5mm [color="Red (633nm)" package="5 mm [THT]"]
  amarelo = LED - 5mm [color="Red (633nm)" package="5 mm [THT]"]
  vermelho = LED - 5mm [color="Red (633nm)" package="5 mm [THT]"]
  on/off = LED - 5mm [color="Red (633nm)" package="5 mm [THT]"]
  azul = LED - 5mm [color="Red (633nm)" package="5 mm [THT]"]
  branco = LED - 5mm [color="Red (633nm)" package="5 mm [THT]"]
  R1 = PHOTOCELL [package=photocell]
  R2 = Resistor [tolerance=±5% resistance=220 package="0402 [SMD]"]
  R3 = Resistor [tolerance=±5% resistance=220 package="0402 [SMD]"]
  R4 = Resistor [tolerance=±5% resistance=220 package="0402 [SMD]"]
  R5 = Resistor [tolerance=±5% resistance=220 package="0402 [SMD]"]
  R6 = Resistor [tolerance=±5% resistance=220 package="0402 [SMD]"]
  R7 = Resistor [tolerance=±5% resistance=220 package="0402 [SMD]"]
  pulldown = Resistor [tolerance=±5% resistance=10k package=THT]
  Componente1 = Arduino Uno (Rev3)
  RHT1 = Humidity and Temperature Sensor RHT03
  pullup = Resistor [tolerance=±5% resistance=10k package=THT]
  detector_som = GAS_SENSOR [package=mq-3]

nets:
  GND: verde.cathode, amarelo.cathode, vermelho.cathode, on/off.cathode, azul.cathode, branco.cathode, pulldown.Pin_1, Componente1.GND, RHT1.GND_2, detector_som.B1
  N1: verde.anode, R7.Pin_1
  N2: amarelo.anode, R6.Pin_1
  N3: vermelho.anode, R5.Pin_1
  N4: on/off.anode, R4.Pin_1
  N5: azul.anode, R3.Pin_1
  N6: branco.anode, R2.Pin_1
  5V: R1.P$1, Componente1.5V, RHT1.Vcc, pullup.Pin_0, detector_som.H1
  N7: R1.P$2, pulldown.Pin_0
  N8: R2.Pin_0, Componente1.D3_PWM
  N9: R3.Pin_0, Componente1.D5_PWM
  N10: R4.Pin_0, Componente1.D4
  N11: R5.Pin_0, Componente1.D2
  N12: R6.Pin_0, Componente1.D1/TX
  N13: R7.Pin_0, Componente1.D0/RX
  N14: Componente1.A0, RHT1.Data-signal, pullup.Pin_1
  N15: Componente1.A1, detector_som.A1
